// Logisim project lab10.circ as structural Verilog: 2 circuits, main circuit main
module main (
  input  clk,
  output Qa,
  output Qb,
  output Qc,
  output Qd,
  output Rc
);

  wire fd_1_qn, fd_2_qn, fd_3_qn, fd_4_qn, nor_1_out, not_1_out, not_2_out, not_3_out, not_4_out, or_1_out,
       xor_1_out, xor_2_out, xor_3_out;

  not not_1 (not_1_out, fd_1_qn);
  nor nor_1 (nor_1_out, fd_1_qn, fd_2_qn);
  or or_1 (or_1_out, fd_1_qn, fd_3_qn, fd_2_qn);
  xor xor_1 (xor_1_out, not_1_out, fd_2_qn);
  xor xor_2 (xor_2_out, nor_1_out, fd_3_qn);
  not not_2 (not_2_out, xor_1_out);
  not not_3 (not_3_out, xor_2_out);
  xor xor_3 (xor_3_out, or_1_out, fd_4_qn);
  not not_4 (not_4_out, xor_3_out);
  FD fd_1 (.D(fd_1_qn), .clk(clk), .Q(Qa), .Qn(fd_1_qn));
  FD fd_2 (.D(not_2_out), .clk(clk), .Q(Qb), .Qn(fd_2_qn));
  FD fd_3 (.D(not_3_out), .clk(clk), .Q(Qc), .Qn(fd_3_qn));
  FD fd_4 (.D(not_4_out), .clk(clk), .Q(Qd), .Qn(fd_4_qn));
  nor nor_2 (Rc, fd_4_qn, fd_3_qn, fd_2_qn, fd_1_qn);
endmodule

module FD (
  input  D,
  input  clk,
  output Q,
  output Qn
);
endmodule
