// Logisim project lab5.circ as structural Verilog
module D_74LS138 (
  input  A,
  input  B,
  input  C,
  input  G,
  input  G2A,
  input  G2B,
  output [7:0] Y
);

  wire and_1_out, and_2_out, and_3_out, and_4_out, nor_1_out, not_1_out, not_2_out, not_3_out, not_4_out;

  not not_1 (not_1_out, A);
  not not_2 (not_2_out, B);
  not not_3 (not_3_out, G);
  nor nor_1 (nor_1_out, not_3_out, G2A, G2B);
  not not_4 (not_4_out, C);
  and and_1 (and_1_out, not_1_out, not_2_out);
  and and_2 (and_2_out, A, not_2_out);
  and and_3 (and_3_out, not_1_out, B);
  and and_4 (and_4_out, A, B);
  nand nand_1 (Y[0], and_1_out, not_4_out, nor_1_out);
  nand nand_2 (Y[1], and_2_out, not_4_out, nor_1_out);
  nand nand_3 (Y[2], and_3_out, not_4_out, nor_1_out);
  nand nand_4 (Y[3], and_4_out, not_4_out, nor_1_out);
  nand nand_5 (Y[4], and_1_out, C, nor_1_out);
  nand nand_6 (Y[5], and_2_out, C, nor_1_out);
  nand nand_7 (Y[6], and_3_out, C, nor_1_out);
  nand nand_8 (Y[7], and_4_out, C, nor_1_out);
endmodule

module Lab5_task1 (
  input  A,
  input  B,
  input  C,
  input  G,
  input  G2A,
  input  G2B,
  output FF
);

  wire [7:0] D_y;

  D_74LS138 D (.A(A), .B(B), .C(C), .G(G), .G2A(G2A), .G2B(G2B), .Y(D_y));
  nand nand_1 (FF, D_y[1], D_y[2], D_y[4], D_y[7]);
endmodule
